# Fritzing sketch Semaphore (saved by Fritzing 0.9.0b)
breadboards: 1

parts:
  Part1 = Arduino Leonardo (Rev3b)
  R1 = Resistor [tolerance=±5% resistance=330 package=THT]
  R2 = Resistor [tolerance=±5% resistance=330 package=THT]
  R3 = Resistor [tolerance=±5% resistance=330 package=THT]
  LED4 = LED - 5mm [color="Red (633nm)" package="5 mm [THT]"]
  LED5 = LED - 5mm [color="Yellow (592nm)" package="5 mm [THT]"]
  LED6 = LED - 5mm [color="Green (565nm)" package="5 mm [THT]"]
  LED7 = LED - 5mm [color="Red (633nm)" package="5 mm [THT]"]
  LED8 = LED - 5mm [color="Green (565nm)" package="5 mm [THT]"]
  R4 = Resistor [tolerance=±5% resistance=330 package=THT]  # not connected
  R5 = Resistor [tolerance=±5% resistance=330 package=THT]
  J1 = Piezo Speaker
  R6 = Trimmer Potentiometer [maximum_resistance=10kΩ package=THT]

nets:
  N1: Part1.D2/SDA, R5.Pin_0
  N2: Part1.D5_PWM, R3.Pin_0
  N3: Part1.D6_PWM/A7, R2.Pin_0
  N4: Part1.D7, R1.Pin_0
  N5: Part1.GND, LED4.anode, LED5.anode, LED6.anode, LED7.anode, LED8.anode, J1.pin1
  N6: Part1.D8/A8, R6.leg1
  N7: R1.Pin_1, LED4.cathode
  N8: R2.Pin_1, LED5.cathode
  N9: R3.Pin_1, LED6.cathode
  N10: LED8.cathode, R5.Pin_1
  N11: J1.pin2, R6.wiper
